// Digital circuit 4-bit.dig as structural Verilog
module _4_bit (
  input  [3:0] A,
  input  [3:0] B,
  output [3:0] Sum
);

  wire cin_1_carry_out, cin_2_carry_out, cin_3_carry_out, cin_4_carry_out;

  cin cin_1 (.A(A[3]), .B(B[3]), .Carry_in(cin_2_carry_out), .Sum(Sum[3]), .Carry_out(cin_1_carry_out));
  cin cin_2 (.A(A[2]), .B(B[2]), .Carry_in(cin_3_carry_out), .Sum(Sum[2]), .Carry_out(cin_2_carry_out));
  cin cin_3 (.A(A[1]), .B(B[1]), .Carry_in(cin_4_carry_out), .Sum(Sum[1]), .Carry_out(cin_3_carry_out));
  cin cin_4 (.A(A[0]), .B(B[0]), .Carry_in(1'b0), .Sum(Sum[0]), .Carry_out(cin_4_carry_out));
endmodule
