// Digital circuit cin.dig as structural Verilog
module cin (
  input  A,
  input  B,
  input  Carry_in,
  output Sum,
  output Carry_out
);

  wire and_1_out, and_2_out, and_3_out, and_4_out, and_5_out, and_6_out, not_1_out, not_2_out, not_3_out,
       not_4_out, or_1_out;

  not not_1 (not_1_out, A);
  not not_2 (not_2_out, B);
  and and_1 (and_1_out, not_1_out, B);
  and and_2 (and_2_out, A, not_2_out);
  and and_3 (and_3_out, A, B);
  or or_1 (or_1_out, and_2_out, and_1_out);
  and and_4 (and_4_out, Carry_in, or_1_out);
  not not_3 (not_3_out, Carry_in);
  not not_4 (not_4_out, or_1_out);
  and and_5 (and_5_out, or_1_out, not_3_out);
  and and_6 (and_6_out, not_4_out, Carry_in);
  or or_2 (Carry_out, and_3_out, and_4_out);
  or or_3 (Sum, and_5_out, and_6_out);
endmodule
